// Logisim project elevator.circ as structural Verilog: 1 circuit, main circuit main
module main (
);

  wire button_1_out, clock_1_out, counter_1_carry, decoder_1_out0, decoder_1_out1, decoder_1_out2,
       decoder_1_out3, decoder_1_out4, decoder_1_out5, decoder_1_out6, decoder_1_out7, or_1_out, or_2_out,
       or_3_out, or_4_out, or_5_out, or_6_out, or_7_out;
  wire [2:0] counter_1_q, undriven;

  or or_1 (or_1_out, decoder_1_out6, decoder_1_out4, decoder_1_out5, decoder_1_out7, decoder_1_out2, decoder_1_out3, decoder_1_out4);
  or or_2 (or_2_out, decoder_1_out7, decoder_1_out0, decoder_1_out2, decoder_1_out5, decoder_1_out6, decoder_1_out3);
  _7_Segment_Display u_7_segment_display_1 (
    .g(or_1_out), .f(or_3_out), .a(or_2_out), .b(or_4_out), .e(or_5_out), .d(or_6_out), .c(or_7_out));  // open: dp
  or or_3 (or_3_out, decoder_1_out0, decoder_1_out1, decoder_1_out4, decoder_1_out6, decoder_1_out5);
  or or_4 (or_4_out, decoder_1_out0, decoder_1_out7, decoder_1_out3, decoder_1_out4, decoder_1_out2, decoder_1_out7);
  or or_5 (or_5_out, decoder_1_out1, decoder_1_out0, decoder_1_out2, decoder_1_out6);
  or or_6 (or_6_out, decoder_1_out0, decoder_1_out2, decoder_1_out3, decoder_1_out5, decoder_1_out6);
  or or_7 (or_7_out, decoder_1_out0, decoder_1_out3, decoder_1_out4, decoder_1_out5, decoder_1_out6, decoder_1_out6, decoder_1_out7);
  Decoder #(.select(3), .tristate("true")) decoder_1 (
    .out0(decoder_1_out0), .out1(decoder_1_out1), .out2(decoder_1_out2), .out3(decoder_1_out3),
    .out4(decoder_1_out4), .out5(decoder_1_out5), .out6(decoder_1_out6), .out7(decoder_1_out7),
    .sel(counter_1_q), .en(1'b1));
  Clock clock_1 (.out(clock_1_out));
  Counter #(.width(3), .max('h7)) counter_1 (
    .D(undriven), .count(1'b1), .Q(counter_1_q), .carry(counter_1_carry), .clk(clock_1_out),
    .clr(button_1_out));  // open: load
  Button button_1 (.out(button_1_out));

  // Notes on the sheet:
  //   Opens the door and clears the pressed button
  //   Current Floor
  //   UP BUTTON
  //   EMERGENCY EXIT
  //   If it's Equals to logic 
  //   the elevator's floor becomes
  //   the 0
  //   COUNTER
  //   DOWN BUTTON
  //   1
  //   Next floor
endmodule
